# Fritzing sketch opz_artnet_adapter (saved by Fritzing 0.9.4)
breadboards: 1

parts:
  S2 = Pushbutton [package="[THT]"]
  Part1 = FTDI Basic Programmer
  U1 = ESP8266 WiFi Module [part_number=ESP8266]
  R1 = Resistor [tolerance=±5% resistance=1k package="1206 [SMD]"]
  R3 = Resistor [tolerance=±5% resistance=1k package="1206 [SMD]"]
  R2 = Resistor [tolerance=±5% resistance=1k package="1206 [SMD]"]
  C1 = Tantalum Capacitor [capacitance=10µF package="D 7343 [SMD, tantalum]"]

nets:
  N1: S2.Pin_1, S2.Pin_2, U1.GPIO_0, R3.Pin_1
  GND: S2.Pin_3, S2.Pin_4, Part1.GND, U1.GND, C1.-
  N2: Part1.RXI, U1.TXD
  N3: Part1.TXO, U1.RXD
  N4: Part1.POWER, U1.VCC, U1.CH_PD, R1.Pin_0, R3.Pin_0, R2.Pin_0, C1.+
  N5: U1.GPIO_16, R1.Pin_1
  N6: U1.GPIO_2, R2.Pin_1

custom parts:
  ESP8266 WiFi Module: Generic WiFi Module based on the ESP8266 with onboard PCB antenna and UART communications
